// Logisim project Ivchenkov.circ as structural Verilog: 4 circuits, main circuit Counter
module Counter (
  output Q0,
  output Q1,
  output Q2,
  output Q3
);

  wire and_1_out, not_1_out, not_2_out, not_3_out, not_4_out, T_2_q, T_3_q, T_4_q, T_q, x1_1_out;

  Clock x1_1 (.out(x1_1_out));
  not not_1 (not_1_out, x1_1_out);
  and and_1 (and_1_out, ~T_q, T_2_q, T_3_q, T_4_q);  // AND_Gate
  T T (.T(1'b1), .C(not_1_out), .Q(T_q), .nQ(Q0));  // open: Save
  not not_2 (not_2_out, Q0);
  T T_2 (.T(1'b1), .C(not_2_out), .Save(and_1_out), .Q(T_2_q), .nQ(Q1));
  T T_3 (.T(1'b1), .C(not_3_out), .Q(T_3_q), .nQ(Q2));  // open: Save
  not not_3 (not_3_out, Q1);
  not not_4 (not_4_out, Q2);
  T T_4 (.T(1'b1), .C(not_4_out), .Q(T_4_q), .nQ(Q3));  // open: Save
  Hex_Digit_Display hex_digit_display_1 (.value({Q3, Q2, Q1, Q0}));  // open: dp
endmodule

module RS (
  input  R,
  input  C,
  input  S,
  output Q,
  output nQ
);

  wire and_1_out, and_2_out;

  and and_1 (and_1_out, R, C);
  and and_2 (and_2_out, C, S);
  nor nor_1 (Q, and_1_out, nQ);
  nor nor_2 (nQ, Q, and_2_out);
endmodule

module JK (
  input  K,
  input  C,
  input  J,
  output Q,
  output nQ
);

  wire and_1_out, and_2_out, not_1_out, not_2_out, not_3_out, or_1_out, or_2_out, or_3_out, Reset_out, RS_nq,
       RS_q;

  and and_1 (and_1_out, not_1_out, K);
  and and_2 (and_2_out, J, or_3_out);
  Button Reset (.out(Reset_out));
  not not_1 (not_1_out, or_1_out);
  RS RS (.R(and_1_out), .C(C), .S(and_2_out), .Q(RS_q), .nQ(RS_nq));
  not not_2 (not_2_out, C);
  or or_1 (or_1_out, not_3_out, Reset_out);
  or or_2 (or_2_out, not_2_out, Reset_out);
  or or_3 (or_3_out, nQ, Reset_out);
  not not_3 (not_3_out, Q);
  RS RS_2 (.R(RS_nq), .C(or_2_out), .S(RS_q), .Q(Q), .nQ(nQ));
endmodule

module T (
  input  T,
  input  C,
  input  Save,
  output Q,
  output nQ
);

  wire and_1_out, xor_1_out;

  xor xor_1 (xor_1_out, C, and_1_out);
  and and_1 (and_1_out, Save, nQ);
  JK JK (.K(T), .C(xor_1_out), .J(T), .Q(Q), .nQ(nQ));
endmodule
